// Logisim project project3.circ as structural Verilog: 2 circuits, main circuit main
// T0
module main (
  input  in_1,
  output [15:0] out_2
);

  wire clock_1_out, IR_EN, IR_LH, MEM_LD, MEM_SEL, T0, T1, T2, T3, T4, T5, T6, T7;
  wire [1:0] _3RB_FS, IR_FS, MuxASel, MuxBSel, OutCSel, OutDSel;
  wire [3:0] _3RB_RS;

  counter counter_1 (
    .out_2(T0), .out_3(T1), .out_4(T2), .out_5(T3), .out_6(T4), .out_7(T5), .out_8(T6), .out_9(T7),
    .in_1(in_1));
  assign OutCSel = T0 ? 2'b00 : 2'bz;  // Controlled_Buffer controlled_buffer_1
  assign OutDSel = T0 ? 2'b01 : 2'bz;  // Controlled_Buffer controlled_buffer_2
  assign _3RB_FS = T0 ? 2'b01 : 2'bz;  // Controlled_Buffer controlled_buffer_3
  assign _3RB_RS = T0 ? 4'b0010 : 4'bz;  // Controlled_Buffer controlled_buffer_4
  assign MuxASel = T0 ? 2'b10 : 2'bz;  // Controlled_Buffer controlled_buffer_5
  assign MuxBSel = T0 ? 2'b11 : 2'bz;  // Controlled_Buffer controlled_buffer_6
  assign MEM_SEL = T1 ? 1'b1 : 1'bz;  // Controlled_Buffer controlled_buffer_7
  assign MEM_LD = T1 ? 1'b1 : 1'bz;  // Controlled_Buffer controlled_buffer_8
  assign _3RB_FS = T1 ? 2'b10 : 2'bz;  // Controlled_Buffer controlled_buffer_9
  assign _3RB_RS = T1 ? 4'b0011 : 4'bz;  // Controlled_Buffer controlled_buffer_10
  assign IR_EN = T1 ? 1'b1 : 1'bz;  // Controlled_Buffer controlled_buffer_11
  assign IR_FS = T1 ? 2'b11 : 2'bz;  // Controlled_Buffer controlled_buffer_12
  assign IR_LH = T1 ? 1'b0 : 1'bz;  // Controlled_Buffer controlled_buffer_13
  assign IR_LH = T2 ? 1'b1 : 1'bz;  // Controlled_Buffer controlled_buffer_14
  assign _3RB_RS = T2 ? 4'b0001 : 4'bz;  // Controlled_Buffer controlled_buffer_15
  assign IR_EN = T3 ? 1'b0 : 1'bz;  // Controlled_Buffer controlled_buffer_16
  Clock clock_1 (.out(clock_1_out));
  part2_main main_1 (
    .MuxASel(MuxASel), .OutCSel(OutCSel), .OutDSel(OutDSel), .FunSel_3(_3RB_FS), .RegSel_2(_3RB_RS),
    .L_H(IR_LH), .Enable(IR_EN), .FunSel_4(IR_FS), .MuxBSel(MuxBSel), .in_11(MEM_SEL), .in_12(MEM_LD),
    .out_23(out_2), .in_2(clock_1_out));  // open: OutASel, OutBSel, FunSel_2, RegSel, MuxCSel, FunSel, out_21, in_10, in_13, out_22
  Hex_Digit_Display hex_digit_display_1 (.value(out_2[15:12]));  // open: dp
  Hex_Digit_Display hex_digit_display_2 (.value(out_2[7:4]));  // open: dp
  Hex_Digit_Display hex_digit_display_3 (.value(out_2[11:8]));  // open: dp
  Hex_Digit_Display hex_digit_display_4 (.value(out_2[3:0]));  // open: dp

  // Other names for the same wires on the sheet: SCR = in_1
endmodule

module counter (
  input  in_1,
  output out_2,
  output out_3,
  output out_4,
  output out_5,
  output out_6,
  output out_7,
  output out_8,
  output out_9
);

  wire clock_1_out;
  wire [2:0] counter_1_q;

  Counter #(.width(3), .max('h7)) counter_1 (
    .Q(counter_1_q), .clk(clock_1_out), .clr(in_1));  // open: load, D, count, carry
  Clock clock_1 (.out(clock_1_out));
  Decoder #(.select(3), .enable("false")) decoder_1 (
    .out0(out_2), .out1(out_3), .out2(out_4), .out3(out_5), .out4(out_6), .out5(out_7), .out6(out_8),
    .out7(out_9), .sel(counter_1_q));
endmodule
